// Logisim project CPU.circ as structural Verilog: 1 circuit, main circuit Ida CPU
// CPU
module Ida_CPU (
  input  [31:0] Instruction,
  input  Clock,
  output [23:0] Mem_Data,
  output [23:0] Mem_Address,
  output Mem_Write,
  output [23:0] Next_PC,
  output [23:0] r00,
  output [23:0] r01,
  output [23:0] r02,
  output [23:0] r03,
  output [23:0] r04,
  output [23:0] r05,
  output [23:0] r06,
  output [23:0] r07,
  output [23:0] r08,
  output [23:0] r09,
  output [23:0] r10,
  output [23:0] r11,
  output [23:0] r12,
  output [23:0] r13,
  output [23:0] r14,
  output [23:0] r15
);

  wire and_5_out, and_6_out, comparator_1_eq, comparator_2_eq, demultiplexer_1_out0, demultiplexer_1_out1,
       demultiplexer_1_out2, demultiplexer_1_out3, demultiplexer_1_out4, demultiplexer_1_out5,
       demultiplexer_1_out6, demultiplexer_1_out7, demultiplexer_1_out8, demultiplexer_1_out9,
       demultiplexer_1_out10, demultiplexer_1_out14, demultiplexer_2_out10, demultiplexer_2_out11,
       demultiplexer_3_out15, demultiplexer_4_out12, demultiplexer_4_out13, do_it, jump, lw, not_1_out,
       not_2_out, not_3_out, or_1_out, or_2_out, or_3_out, or_4_out, RegWrite;
  wire [2:0] comp, CQ, curr_comp;
  wire [3:0] A3RS, RI, WriteReg;
  wire [15:0] A3I, bit_extender_2_out;
  wire [19:0] bit_extender_3_out;
  wire [23:0] adder_1_out, bit_extender_4_out, bit_extender_5_out, immediate, mem_out, memDatal,
       multiplexer_7_out, RI_val, RS_val, s1, s2, WriteVal;
  wire [31:20] delayed_Inst;

  // Probe on Instruction
  // Probe on Clock
  // Probe on r00
  // Probe on r01
  // Probe on r02
  // Probe on r03
  // Probe on r04
  // Probe on r05
  // Probe on r06
  // Probe on r07
  Demultiplexer #(.select(4)) demultiplexer_1 (
    .out0(demultiplexer_1_out0), .out1(demultiplexer_1_out1), .out2(demultiplexer_1_out2),
    .out3(demultiplexer_1_out3), .out4(demultiplexer_1_out4), .out5(demultiplexer_1_out5),
    .out6(demultiplexer_1_out6), .out7(demultiplexer_1_out7), .out8(demultiplexer_1_out8),
    .out9(demultiplexer_1_out9), .out10(demultiplexer_1_out10), .out14(demultiplexer_1_out14), .in(1'b1),
    .sel(delayed_Inst[31:28]));  // open: out11, out12, out13, out15, en
  // Probe on Mem_Data
  // Probe on Mem_Address
  // Probe on Mem_Write
  // Probe on Next_PC
  Register #(.width(32)) register_1 (
    .D(Instruction), .Q({delayed_Inst[31:28], CQ, delayed_Inst[24:20], A3RS, A3I}), .clk(Clock));  // open: en, clr
  Bit_Extender #(.in_width(24), .out_width(4)) bit_extender_1 (.in({delayed_Inst[23:20], A3RS, A3I}), .out(RI));
  or or_1 (or_1_out, demultiplexer_1_out0, demultiplexer_1_out1, demultiplexer_1_out2, demultiplexer_1_out3, demultiplexer_1_out4);
  or or_2 (or_2_out, demultiplexer_1_out5, demultiplexer_1_out6, demultiplexer_1_out7, demultiplexer_1_out8, demultiplexer_1_out9);
  // Probe on r08
  // Probe on r09
  // Probe on r10
  // Probe on r11
  // Probe on r12
  // Probe on r13
  // Probe on r14
  // Probe on r15
  or or_3 (or_3_out, or_1_out, or_2_out, demultiplexer_1_out10, demultiplexer_1_out14);
  and and_1 (RegWrite, do_it, or_3_out);
  Demultiplexer #(.select(4)) demultiplexer_2 (
    .out10(demultiplexer_2_out10), .out11(demultiplexer_2_out11), .in(1'b1), .sel(delayed_Inst[31:28]));  // open: out0, out1, out2, out3, out4, out5, out6, out7, out8, out9, out12, out13, out14, out15, en
  Bit_Extender #(.in_width(24)) bit_extender_2 (.in({delayed_Inst[23:20], A3RS, A3I}), .out(bit_extender_2_out));
  Bit_Extender #(.in_width(24), .out_width(20)) bit_extender_3 (
    .in({delayed_Inst[23:20], A3RS, A3I}), .out(bit_extender_3_out));
  assign bit_extender_4_out = {{8{bit_extender_2_out[15]}}, bit_extender_2_out};  // Bit_Extender bit_extender_4
  assign bit_extender_5_out = {{4{bit_extender_3_out[19]}}, bit_extender_3_out};  // Bit_Extender bit_extender_5
  Demultiplexer #(.select(4)) demultiplexer_3 (
    .out15(demultiplexer_3_out15), .in(1'b1), .sel(delayed_Inst[31:28]));  // open: out0, out1, out2, out3, out4, out5, out6, out7, out8, out9, out10, out11, out12, out13, out14, en
  and and_2 (lw, do_it, demultiplexer_2_out10);
  and and_3 (Mem_Write, do_it, demultiplexer_2_out11);
  Ida_Register_File ida_register_file_1 (
    .Read_Reg_1(RI), .Read_Reg_2(A3RS), .Write_Reg(WriteReg), .Write_Value(WriteVal), .Reg_1_Value(RI_val),
    .Reg_2_Value(RS_val), .Reg_Write(RegWrite), .Clock(Clock), .r00(r00), .r01(r01), .r02(r02), .r03(r03),
    .r04(r04), .r05(r05), .r06(r06), .r07(r07), .r08(r08), .r09(r09), .r10(r10), .r11(r11), .r12(r12),
    .r13(r13), .r14(r14), .r15(r15), .Reg_3_Value(Mem_Data));
  Multiplexer #(.select(4), .width(24)) multiplexer_1 (
    .in0(bit_extender_4_out), .in1(bit_extender_4_out), .in2(bit_extender_4_out), .in3(bit_extender_4_out),
    .in4(bit_extender_4_out), .in5(bit_extender_4_out), .in6(bit_extender_4_out), .in7(bit_extender_4_out),
    .in8(bit_extender_4_out), .in9(bit_extender_4_out), .in10(bit_extender_4_out), .in11(bit_extender_4_out),
    .in12(bit_extender_5_out), .in13(bit_extender_5_out), .in14({delayed_Inst[23:20], A3RS, A3I}),
    .in15({delayed_Inst[23:20], A3RS, A3I}), .out(immediate), .sel(delayed_Inst[31:28]));  // open: en
  and and_4 (jump, do_it, demultiplexer_3_out15);
  Multiplexer #(.width(4)) multiplexer_2 (
    .in0(delayed_Inst[23:20]), .in1(4'b0010), .out(WriteReg), .sel(comparator_1_eq));  // open: en
  Comparator #(.width(4)) comparator_1 (.a(delayed_Inst[31:28]), .b(4'b1110), .eq(comparator_1_eq));  // open: gt, lt
  Demultiplexer #(.select(4)) demultiplexer_4 (
    .out12(demultiplexer_4_out12), .out13(demultiplexer_4_out13), .in(1'b1), .sel(delayed_Inst[31:28]));  // open: out0, out1, out2, out3, out4, out5, out6, out7, out8, out9, out10, out11, out14, out15, en
  Multiplexer #(.width(24)) multiplexer_3 (
    .in0(RI_val), .in1(immediate), .out(s2), .sel(delayed_Inst[24]));  // open: en
  and and_5 (and_5_out, or_4_out, do_it);
  or or_4 (or_4_out, demultiplexer_4_out12, demultiplexer_4_out13, 1'b0);
  Ida_ALU ida_alu_1 (.ALU_Source_1(s1), .ALU_Source_2(s2), .Operation(delayed_Inst[31:28]), .ALU_Result(Mem_Address));
  Register #(.width(3)) comparison (.D(comp), .en(and_5_out), .Q(curr_comp), .clk(Clock));  // open: clr
  // Probe on {delayed_Inst[31:28], CQ, delayed_Inst[24:20], A3RS, A3I}
  // Probe on Mem_Data
  // Probe on mem_out
  // Probe on delayed_Inst[31:28]
  Multiplexer #(.select(4), .width(24)) multiplexer_4 (
    .in0(RS_val), .in1(RS_val), .in2(RS_val), .in3(RS_val), .in4(RS_val), .in5(RS_val), .in6(RS_val),
    .in7(RS_val), .in8(RS_val), .in9(RS_val), .in10(RS_val), .in11(RS_val), .in12(Mem_Data), .in13(Mem_Data),
    .in14({24{1'b0}}), .in15({24{1'b0}}), .out(s1), .sel(delayed_Inst[31:28]));  // open: en
  RAM #(.addrWidth(24), .dataWidth(24), .bus("separate")) ram_1 (
    .addr(Mem_Address), .din(memDatal), .data(mem_out), .str(Mem_Write), .clk(Clock));  // open: sel, ld, clr
  not not_1 (not_1_out, curr_comp[0]);
  not not_2 (not_2_out, curr_comp[1]);
  not not_3 (not_3_out, curr_comp[2]);
  // Probe on Mem_Address
  // Probe on WriteVal
  Bit_Extender #(.in_width(24), .out_width(3)) bit_extender_6 (.in(Mem_Address), .out(comp));
  Multiplexer #(.select(3)) multiplexer_5 (
    .in0(1'b0), .in1(not_1_out), .in2(curr_comp[0]), .in3(not_2_out), .in4(curr_comp[1]), .in5(not_3_out),
    .in6(curr_comp[2]), .in7(1'b1), .out(do_it), .sel(CQ));  // open: en
  Adder #(.width(24)) adder_1 (.a(Next_PC), .b(24'h1), .out(adder_1_out));  // open: cin, cout
  Comparator #(.width(4)) comparator_2 (.a(delayed_Inst[31:28]), .b(4'b1111), .eq(comparator_2_eq));  // open: gt, lt
  Multiplexer #(.select(4), .width(24)) multiplexer_6 (
    .in0(Mem_Address), .in1(Mem_Address), .in2(Mem_Address), .in3(Mem_Address), .in4(Mem_Address),
    .in5(Mem_Address), .in6(Mem_Address), .in7(Mem_Address), .in8(Mem_Address), .in9(Mem_Address),
    .in10(mem_out), .in11({24{1'b0}}), .in12({24{1'b0}}), .in13({24{1'b0}}), .in14({24{1'b0}}),
    .in15({24{1'b0}}), .out(WriteVal), .sel(delayed_Inst[31:28]));  // open: en
  Multiplexer #(.width(24)) multiplexer_7 (
    .in0(adder_1_out), .in1(immediate), .out(multiplexer_7_out), .sel(and_6_out));  // open: en
  and and_6 (and_6_out, comparator_2_eq, do_it);
  Register #(.width(24)) PC (.D(multiplexer_7_out), .Q(Next_PC), .clk(Clock));  // open: en, clr

  // Other names for the same wires on the sheet: clk = Clock; tunnel_t_t = curr_comp[0]; tunnel_t = curr_comp[1];
  //   tunnel = curr_comp[2]; delayed_Inst (some bits) = {CQ, A3RS, A3I};
  //   registers[23:0] = {delayed_Inst[23:20], A3RS, A3I}; RD[3:0] = delayed_Inst[23:20]; IMM = delayed_Inst[24];
  //   op[3:0] = delayed_Inst[31:28]; inst[31:0] = Instruction; ALU_out[23:0] = Mem_Address;
  //   memAddr[23:0] = Mem_Address; memData[23:0] = Mem_Data; memWrite = Mem_Write; nextPC[23:0] = Next_PC

  // Notes on the sheet:
  //   INPUTS
  //   INPUT PROBES
  //   OUTPUT PROBES
  //   OUTPUTS
  //   DO NOT MOVE/ADD/CHANGE ANY INPUT OR OUTPUT PINS!
endmodule
