// Logisim project REG.circ as structural Verilog
// Register File
module Ida_Register_File (
  input  [3:0] Read_Reg_1,
  input  [3:0] Read_Reg_2,
  input  [3:0] Write_Reg,
  input  [23:0] Write_Value,
  input  Reg_Write,
  input  Clock,
  output [23:0] Reg_1_Value,
  output [23:0] Reg_2_Value,
  output [23:0] Reg_3_Value,
  output [23:0] r00,
  output [23:0] r01,
  output [23:0] r02,
  output [23:0] r03,
  output [23:0] r04,
  output [23:0] r05,
  output [23:0] r06,
  output [23:0] r07,
  output [23:0] r08,
  output [23:0] r09,
  output [23:0] r10,
  output [23:0] r11,
  output [23:0] r12,
  output [23:0] r13,
  output [23:0] r14,
  output [23:0] r15
);

  wire and_1_out, and_2_out, and_3_out, and_4_out, and_5_out, and_6_out, and_7_out, and_8_out, and_9_out,
       and_10_out, and_11_out, and_12_out, and_13_out, and_14_out, and_15_out, demultiplexer_1_out1,
       demultiplexer_1_out2, demultiplexer_1_out3, demultiplexer_1_out4, demultiplexer_1_out5,
       demultiplexer_1_out6, demultiplexer_1_out7, demultiplexer_1_out8, demultiplexer_1_out9,
       demultiplexer_1_out10, demultiplexer_1_out11, demultiplexer_1_out12, demultiplexer_1_out13,
       demultiplexer_1_out14, demultiplexer_1_out15;

  // Probe on Read_Reg_1
  // Probe on Read_Reg_2
  // Probe on Write_Reg
  // Probe on Write_Value
  // Probe on Reg_Write
  // Probe on Clock
  // Probe on Reg_1_Value
  // Probe on Reg_2_Value
  // Probe on Reg_3_Value
  // Probe on {24{1'b0}}
  // Probe on r01
  // Probe on r02
  // Probe on r03
  // Probe on r04
  // Probe on r05
  // Probe on r06
  // Probe on r07
  // Probe on r08
  // Probe on r09
  // Probe on r10
  // Probe on r11
  // Probe on r12
  // Probe on r13
  // Probe on r14
  // Probe on r15
  Multiplexer #(.select(4), .width(24)) multiplexer_1 (
    .in0({24{1'b0}}), .in1(r01), .in2(r02), .in3(r03), .in4(r04), .in5(r05), .in6(r06), .in7(r07), .in8(r08),
    .in9(r09), .in10(r10), .in11(r11), .in12(r12), .in13(r13), .in14(r14), .in15(r15), .out(Reg_1_Value),
    .sel(Read_Reg_1));  // open: en
  and and_1 (and_1_out, Reg_Write, demultiplexer_1_out8);
  and and_2 (and_2_out, Reg_Write, demultiplexer_1_out7);
  and and_3 (and_3_out, Reg_Write, demultiplexer_1_out6);
  and and_4 (and_4_out, Reg_Write, demultiplexer_1_out5);
  and and_5 (and_5_out, Reg_Write, demultiplexer_1_out4);
  and and_6 (and_6_out, Reg_Write, demultiplexer_1_out3);
  and and_7 (and_7_out, Reg_Write, demultiplexer_1_out2);
  and and_8 (and_8_out, Reg_Write, demultiplexer_1_out1);
  Register #(.width(24)) register_1 (.D(Write_Value), .en(and_1_out), .Q(r08), .clk(Clock));  // open: clr
  Register #(.width(24)) register_2 (.D(Write_Value), .en(and_2_out), .Q(r07), .clk(Clock));  // open: clr
  Register #(.width(24)) register_3 (.D(Write_Value), .en(and_3_out), .Q(r06), .clk(Clock));  // open: clr
  Register #(.width(24)) register_4 (.D(Write_Value), .en(and_4_out), .Q(r05), .clk(Clock));  // open: clr
  Register #(.width(24)) register_5 (.D(Write_Value), .en(and_5_out), .Q(r04), .clk(Clock));  // open: clr
  Register #(.width(24)) register_6 (.D(Write_Value), .en(and_6_out), .Q(r03), .clk(Clock));  // open: clr
  Register #(.width(24)) register_7 (.D(Write_Value), .en(and_7_out), .Q(r02), .clk(Clock));  // open: clr
  Register #(.width(24)) register_8 (.D(Write_Value), .en(and_8_out), .Q(r01), .clk(Clock));  // open: clr
  Multiplexer #(.select(4), .width(24)) multiplexer_2 (
    .in0({24{1'b0}}), .in1(r01), .in2(r02), .in3(r03), .in4(r04), .in5(r05), .in6(r06), .in7(r07), .in8(r08),
    .in9(r09), .in10(r10), .in11(r11), .in12(r12), .in13(r13), .in14(r14), .in15(r15), .out(Reg_2_Value),
    .sel(Read_Reg_2));  // open: en
  Demultiplexer #(.select(4)) demultiplexer_1 (
    .out1(demultiplexer_1_out1), .out2(demultiplexer_1_out2), .out3(demultiplexer_1_out3),
    .out4(demultiplexer_1_out4), .out5(demultiplexer_1_out5), .out6(demultiplexer_1_out6),
    .out7(demultiplexer_1_out7), .out8(demultiplexer_1_out8), .out9(demultiplexer_1_out9),
    .out10(demultiplexer_1_out10), .out11(demultiplexer_1_out11), .out12(demultiplexer_1_out12),
    .out13(demultiplexer_1_out13), .out14(demultiplexer_1_out14), .out15(demultiplexer_1_out15), .in(1'b1),
    .sel(Write_Reg));  // open: out0, en
  Register #(.width(24)) register_9 (.D(Write_Value), .en(and_15_out), .Q(r09), .clk(Clock));  // open: clr
  Register #(.width(24)) register_10 (.D(Write_Value), .en(and_9_out), .Q(r10), .clk(Clock));  // open: clr
  and and_9 (and_9_out, Reg_Write, demultiplexer_1_out10);
  Register #(.width(24)) register_11 (.D(Write_Value), .en(and_10_out), .Q(r11), .clk(Clock));  // open: clr
  and and_10 (and_10_out, Reg_Write, demultiplexer_1_out11);
  Register #(.width(24)) register_12 (.D(Write_Value), .en(and_11_out), .Q(r12), .clk(Clock));  // open: clr
  and and_11 (and_11_out, Reg_Write, demultiplexer_1_out12);
  Register #(.width(24)) register_13 (.D(Write_Value), .en(and_12_out), .Q(r13), .clk(Clock));  // open: clr
  and and_12 (and_12_out, Reg_Write, demultiplexer_1_out13);
  Register #(.width(24)) register_14 (.D(Write_Value), .en(and_13_out), .Q(r14), .clk(Clock));  // open: clr
  and and_13 (and_13_out, Reg_Write, demultiplexer_1_out14);
  Register #(.width(24)) register_15 (.D(Write_Value), .en(and_14_out), .Q(r15), .clk(Clock));  // open: clr
  and and_14 (and_14_out, Reg_Write, demultiplexer_1_out15);
  and and_15 (and_15_out, Reg_Write, demultiplexer_1_out9);
  Multiplexer #(.select(4), .width(24)) multiplexer_3 (
    .in0({24{1'b0}}), .in1(r01), .in2(r02), .in3(r03), .in4(r04), .in5(r05), .in6(r06), .in7(r07), .in8(r08),
    .in9(r09), .in10(r10), .in11(r11), .in12(r12), .in13(r13), .in14(r14), .in15(r15), .out(Reg_3_Value),
    .sel(Write_Reg));  // open: en

  assign r00 = {24{1'b0}};

  // Other names for the same wires on the sheet: clk = Clock; reg1Read[3:0] = Read_Reg_1; reg1Val[23:0] = Reg_1_Value;
  //   reg2Read[3:0] = Read_Reg_2; reg2Val[23:0] = Reg_2_Value; reg3Val[23:0] = Reg_3_Value;
  //   reg3Write[3:0] = Write_Reg; write = Reg_Write; writeVal[23:0] = Write_Value

  // Notes on the sheet:
  //   INPUT PINS
  //   INPUT PROBES
  //   OUTPUT PROBES
  //   OUTPUT PINS
  //   DO NOT MOVE/ADD/CHANGE ANY INPUT OR OUTPUT PINS!
endmodule

module Writes (
);

  wire and_1_out, and_2_out, and_3_out, and_4_out, and_5_out, and_6_out, and_7_out, and_8_out, and_9_out,
       and_10_out, and_11_out, and_12_out, and_13_out, and_14_out, and_15_out, clk, demultiplexer_1_out1,
       demultiplexer_1_out2, demultiplexer_1_out3, demultiplexer_1_out4, demultiplexer_1_out5,
       demultiplexer_1_out6, demultiplexer_1_out7, demultiplexer_1_out8, demultiplexer_1_out9,
       demultiplexer_1_out10, demultiplexer_1_out11, demultiplexer_1_out12, demultiplexer_1_out13,
       demultiplexer_1_out14, demultiplexer_1_out15, write;
  wire [3:0] reg3Write;
  wire [23:0] R01, R02, R03, R04, R05, R06, R07, R08, R09, R10, R11, R12, R13, R14, R15, writeVal;

  and and_1 (and_1_out, write, demultiplexer_1_out8);
  and and_2 (and_2_out, write, demultiplexer_1_out7);
  and and_3 (and_3_out, write, demultiplexer_1_out6);
  and and_4 (and_4_out, write, demultiplexer_1_out4);
  and and_5 (and_5_out, write, demultiplexer_1_out2);
  and and_6 (and_6_out, write, demultiplexer_1_out5);
  and and_7 (and_7_out, write, demultiplexer_1_out3);
  and and_8 (and_8_out, write, demultiplexer_1_out1);
  Register #(.width(24)) register_1 (.D(writeVal), .en(and_1_out), .Q(R08), .clk(clk));  // open: clr
  Register #(.width(24)) register_2 (.D(writeVal), .en(and_2_out), .Q(R07), .clk(clk));  // open: clr
  Register #(.width(24)) register_3 (.D(writeVal), .en(and_3_out), .Q(R06), .clk(clk));  // open: clr
  Register #(.width(24)) register_4 (.D(writeVal), .en(and_6_out), .Q(R05), .clk(clk));  // open: clr
  Register #(.width(24)) register_5 (.D(writeVal), .en(and_4_out), .Q(R04), .clk(clk));  // open: clr
  Register #(.width(24)) register_6 (.D(writeVal), .en(and_7_out), .Q(R03), .clk(clk));  // open: clr
  Register #(.width(24)) register_7 (.D(writeVal), .en(and_5_out), .Q(R02), .clk(clk));  // open: clr
  Register #(.width(24)) register_8 (.D(writeVal), .en(and_8_out), .Q(R01), .clk(clk));  // open: clr
  Demultiplexer #(.select(4)) demultiplexer_1 (
    .out1(demultiplexer_1_out1), .out2(demultiplexer_1_out2), .out3(demultiplexer_1_out3),
    .out4(demultiplexer_1_out4), .out5(demultiplexer_1_out5), .out6(demultiplexer_1_out6),
    .out7(demultiplexer_1_out7), .out8(demultiplexer_1_out8), .out9(demultiplexer_1_out9),
    .out10(demultiplexer_1_out10), .out11(demultiplexer_1_out11), .out12(demultiplexer_1_out12),
    .out13(demultiplexer_1_out13), .out14(demultiplexer_1_out14), .out15(demultiplexer_1_out15), .in(1'b1),
    .sel(reg3Write));  // open: out0, en
  Register #(.width(24)) register_9 (.D(writeVal), .en(and_9_out), .Q(R09), .clk(clk));  // open: clr
  Register #(.width(24)) register_10 (.D(writeVal), .en(and_10_out), .Q(R10), .clk(clk));  // open: clr
  Register #(.width(24)) register_11 (.D(writeVal), .en(and_11_out), .Q(R11), .clk(clk));  // open: clr
  Register #(.width(24)) register_12 (.D(writeVal), .en(and_12_out), .Q(R12), .clk(clk));  // open: clr
  Register #(.width(24)) register_13 (.D(writeVal), .en(and_13_out), .Q(R13), .clk(clk));  // open: clr
  Register #(.width(24)) register_14 (.D(writeVal), .en(and_14_out), .Q(R14), .clk(clk));  // open: clr
  Register #(.width(24)) register_15 (.D(writeVal), .en(and_15_out), .Q(R15), .clk(clk));  // open: clr
  and and_9 (and_9_out, write, demultiplexer_1_out9);
  and and_10 (and_10_out, write, demultiplexer_1_out10);
  and and_11 (and_11_out, write, demultiplexer_1_out11);
  and and_12 (and_12_out, write, demultiplexer_1_out12);
  and and_13 (and_13_out, write, demultiplexer_1_out13);
  and and_14 (and_14_out, write, demultiplexer_1_out14);
  and and_15 (and_15_out, write, demultiplexer_1_out15);
endmodule

module Read (
);

  wire clk;
  wire [3:0] reg1Read, reg2Read, reg3Read;
  wire [23:0] multiplexer_1_out, multiplexer_2_out, multiplexer_3_out, R00, R01, R02, R03, R04, R05, R06,
       R07, R08, R09, R10, R11, R12, R13, R14, R15, reg1Val, reg2Val, reg3Val;

  Multiplexer #(.select(4), .width(24)) multiplexer_1 (
    .in0(R00), .in1(R01), .in2(R02), .in3(R03), .in4(R04), .in5(R05), .in6(R06), .in7(R07), .in8(R08),
    .in9(R09), .in10(R10), .in11(R11), .in12(R12), .in13(R13), .in14(R14), .in15(R15),
    .out(multiplexer_1_out), .sel(reg1Read));  // open: en
  Register #(.width(24)) register_1 (.D(multiplexer_1_out), .Q(reg1Val), .clk(clk));  // open: en, clr
  Multiplexer #(.select(4), .width(24)) multiplexer_2 (
    .in0(R00), .in1(R01), .in2(R02), .in3(R03), .in4(R04), .in5(R05), .in6(R06), .in7(R07), .in8(R08),
    .in9(R09), .in10(R10), .in11(R11), .in12(R12), .in13(R13), .in14(R14), .in15(R15),
    .out(multiplexer_2_out), .sel(reg2Read));  // open: en
  Register #(.width(24)) register_2 (.D(multiplexer_2_out), .Q(reg2Val), .clk(clk));  // open: en, clr
  Multiplexer #(.select(4), .width(24)) multiplexer_3 (
    .in0(R00), .in1(R01), .in2(R02), .in3(R03), .in4(R04), .in5(R05), .in6(R06), .in7(R07), .in8(R08),
    .in9(R09), .in10(R10), .in11(R11), .in12(R12), .in13(R13), .in14(R14), .in15(R15),
    .out(multiplexer_3_out), .sel(reg3Read));  // open: en
  Register #(.width(24)) register_3 (.D(multiplexer_3_out), .Q(reg3Val), .clk(clk));  // open: en, clr
endmodule
